// Logisim project Main.circ as structural Verilog: 4 circuits, main circuit main
module main (
);

  wire A_2_q0, A_2_q1, A_2_q2, A_2_q3, A_In, A_Out, A_q0, A_q1, A_q2, A_q3, Adder_2_c_out, Adder_2_s0,
       Adder_2_s1, Adder_2_s2, Adder_2_s3, Adder_s0, Adder_s1, Adder_s2, Adder_s3, ALU_Temp_2_q0,
       ALU_Temp_2_q1, ALU_Temp_2_q2, ALU_Temp_2_q3, ALU_Temp_In, ALU_Temp_Out, ALU_Temp_q0, ALU_Temp_q1,
       ALU_Temp_q2, ALU_Temp_q3, and_1_out, and_2_out, and_3_out, and_4_out, B_2_q0, B_2_q1, B_2_q2, B_2_q3,
       B_In, B_q0, B_q1, B_q2, B_q3, C, Carry, clock_1_out, decoder_1_out0, decoder_1_out1, decoder_1_out2,
       decoder_2_out1, decoder_2_out2, decoder_2_out3, Halt, IR_In, IR_q0, IR_q1, IR_q2, IR_q3, MAR_In,
       nor_1_out, nor_2_out, nor_3_out, nor_4_out, not_1_out, not_2_out, Opperand_Out, or_1_out, or_2_out,
       or_3_out, or_4_out, Out_In, PC_Count, PC_In, PC_Out, PC_q0, PC_q1, PC_q2, PC_q3, pull_resistor_1_node,
       RAM_In, RAM_Out, Reset, Run_out, Sub, xor_1_out, xor_2_out, xor_3_out, xor_4_out, xor_5_out,
       xor_6_out, xor_7_out, xor_8_out, Zero;
  wire [3:0] IR_2_q0, MAR_q0, Microstep_Counter_q0, Out_2_q0, Out_q0;
  wire [7:0] controlled_buffer_1_out;
  wire [15:0] rom_1_data;
  wire [15:14] controlled_buffer_9_out;

  Hex_Digit_Display hex_digit_display_1 (.value(IR_2_q0));  // open: dp
  Counter PC (
    .In(PC_In), .Count(PC_Count), .D0(controlled_buffer_1_out[0]), .D1(controlled_buffer_1_out[1]),
    .D2(controlled_buffer_1_out[2]), .D3(controlled_buffer_1_out[3]), .Q0(PC_q0), .Q1(PC_q1), .Q2(PC_q2),
    .Q3(PC_q3), .Zero(Reset));
  Register MAR (
    .D0(controlled_buffer_1_out[0]), .Write(MAR_In), .D1(controlled_buffer_1_out[1]),
    .D2(controlled_buffer_1_out[2]), .D3(controlled_buffer_1_out[3]), .Q0(MAR_q0[0]), .Zero(Reset),
    .Q1(MAR_q0[1]), .Q2(MAR_q0[2]), .Q3(MAR_q0[3]));
  Register IR (
    .D0(controlled_buffer_1_out[0]), .Write(IR_In), .D1(controlled_buffer_1_out[1]),
    .D2(controlled_buffer_1_out[2]), .D3(controlled_buffer_1_out[3]), .Q0(IR_q0), .Zero(Reset), .Q1(IR_q1),
    .Q2(IR_q2), .Q3(IR_q3));
  Register IR_2 (
    .D0(controlled_buffer_1_out[4]), .Write(IR_In), .D1(controlled_buffer_1_out[5]),
    .D2(controlled_buffer_1_out[6]), .D3(controlled_buffer_1_out[7]), .Q0(IR_2_q0[0]), .Zero(Reset),
    .Q1(IR_2_q0[1]), .Q2(IR_2_q0[2]), .Q3(IR_2_q0[3]));
  Pull_Resistor pull_resistor_1 (.node(pull_resistor_1_node));
  Button u_Reset (.out(Reset));
  Button Run (.out(Run_out));
  LED #(.active("false")) u_Halt (.in(Halt));
  or or_1 (or_1_out, RAM_Out, RAM_In);
  not not_1 (not_1_out, RAM_In);
  assign controlled_buffer_1_out[0] = Opperand_Out ? IR_q0 : 1'bz;  // Controlled_Buffer controlled_buffer_1
  assign controlled_buffer_1_out[1] = Opperand_Out ? IR_q1 : 1'bz;  // Controlled_Buffer controlled_buffer_2
  Counter Microstep_Counter (
    .In(pull_resistor_1_node), .Count(and_1_out), .Q0(Microstep_Counter_q0[0]), .Q1(Microstep_Counter_q0[1]),
    .Q2(Microstep_Counter_q0[2]), .Q3(Microstep_Counter_q0[3]), .Zero(or_2_out));  // open: D0, D1, D2, D3
  and and_1 (and_1_out, clock_1_out, Run_out, Halt);
  Clock clock_1 (.out(clock_1_out));
  assign controlled_buffer_1_out[0] = PC_Out ? PC_q0 : 1'bz;  // Controlled_Buffer controlled_buffer_3
  assign controlled_buffer_1_out[1] = PC_Out ? PC_q1 : 1'bz;  // Controlled_Buffer controlled_buffer_4
  assign controlled_buffer_1_out[2] = PC_Out ? PC_q2 : 1'bz;  // Controlled_Buffer controlled_buffer_5
  assign controlled_buffer_1_out[3] = PC_Out ? PC_q3 : 1'bz;  // Controlled_Buffer controlled_buffer_6
  RAM #(.addrWidth(4), .bus("asynch")) ram_1 (
    .addr(MAR_q0), .data(controlled_buffer_1_out), .sel(or_1_out), .ld(not_1_out));  // open: clr
  Register Flags (
    .D0(Adder_2_c_out), .Write(ALU_Temp_In), .D1(nor_4_out), .Q0(Carry), .Q1(Zero));  // open: D2, D3, Zero, Q2, Q3
  assign controlled_buffer_1_out[2] = Opperand_Out ? IR_q2 : 1'bz;  // Controlled_Buffer controlled_buffer_7
  assign controlled_buffer_1_out[3] = Opperand_Out ? IR_q3 : 1'bz;  // Controlled_Buffer controlled_buffer_8
  Decoder #(.select(4), .disabled(0), .enable("false")) decoder_1 (
    .out0(decoder_1_out0), .out1(decoder_1_out1), .out2(decoder_1_out2), .sel(Microstep_Counter_q0));  // open: out3, out4, out5, out6, out7, out8, out9, out10, out11, out12, out13, out14, out15
  nor nor_1 (nor_1_out, decoder_1_out0, decoder_1_out1);
  or or_2 (or_2_out, Reset, and_2_out);
  Pull_Resistor pull_resistor_2 (.node(controlled_buffer_1_out));
  not not_2 (not_2_out, nor_1_out);
  Register A (
    .D0(controlled_buffer_1_out[0]), .Write(A_In), .D1(controlled_buffer_1_out[1]),
    .D2(controlled_buffer_1_out[2]), .D3(controlled_buffer_1_out[3]), .Q0(A_q0), .Zero(Reset), .Q1(A_q1),
    .Q2(A_q2), .Q3(A_q3));
  xor xor_1 (xor_1_out, Sub, B_q1);
  xor xor_2 (xor_2_out, Sub, B_q3);
  xor xor_3 (xor_3_out, Sub, B_q2);
  Register B (
    .D0(controlled_buffer_1_out[0]), .Write(B_In), .D1(controlled_buffer_1_out[1]),
    .D2(controlled_buffer_1_out[2]), .D3(controlled_buffer_1_out[3]), .Q0(B_q0), .Zero(Reset), .Q1(B_q1),
    .Q2(B_q2), .Q3(B_q3));
  nor nor_2 (nor_2_out, decoder_1_out2, not_2_out);
  assign {controlled_buffer_9_out, Sub, ALU_Temp_Out, ALU_Temp_In, Opperand_Out, IR_In, PC_Count, PC_Out, Out_In, B_In, A_Out, A_In, MAR_In, RAM_Out, RAM_In} = decoder_1_out0 ? 16'h84 : 16'bz;  // Controlled_Buffer controlled_buffer_9
  assign {controlled_buffer_9_out, Sub, ALU_Temp_Out, ALU_Temp_In, Opperand_Out, IR_In, PC_Count, PC_Out, Out_In, B_In, A_Out, A_In, MAR_In, RAM_Out, RAM_In} = decoder_1_out1 ? 16'h302 : 16'bz;  // Controlled_Buffer controlled_buffer_10
  assign controlled_buffer_1_out[0] = A_Out ? A_q0 : 1'bz;  // Controlled_Buffer controlled_buffer_11
  assign controlled_buffer_1_out[1] = A_Out ? A_q1 : 1'bz;  // Controlled_Buffer controlled_buffer_12
  assign controlled_buffer_1_out[2] = A_Out ? A_q2 : 1'bz;  // Controlled_Buffer controlled_buffer_13
  Register A_2 (
    .D0(controlled_buffer_1_out[4]), .Write(A_In), .D1(controlled_buffer_1_out[5]),
    .D2(controlled_buffer_1_out[6]), .D3(controlled_buffer_1_out[7]), .Q0(A_2_q0), .Zero(Reset), .Q1(A_2_q1),
    .Q2(A_2_q2), .Q3(A_2_q3));
  Full_Adder Adder (
    .A0(A_q0), .B0(xor_4_out), .C_In(Sub), .A1(A_q1), .B1(xor_1_out), .A2(A_q2), .B2(xor_3_out), .A3(A_q3),
    .B3(xor_2_out), .S0(Adder_s0), .S1(Adder_s1), .S2(Adder_s2), .S3(Adder_s3), .C_Out(C));
  xor xor_4 (xor_4_out, Sub, B_q0);
  xor xor_5 (xor_5_out, Sub, B_2_q3);
  Register B_2 (
    .D0(controlled_buffer_1_out[4]), .Write(B_In), .D1(controlled_buffer_1_out[5]),
    .D2(controlled_buffer_1_out[6]), .D3(controlled_buffer_1_out[7]), .Q0(B_2_q0), .Zero(Reset), .Q1(B_2_q1),
    .Q2(B_2_q2), .Q3(B_2_q3));
  nor nor_3 (nor_3_out, controlled_buffer_9_out[15], controlled_buffer_9_out[14], Sub, ALU_Temp_Out, ALU_Temp_In, Opperand_Out, IR_In, PC_Count, Out_In, B_In, A_Out, A_In, MAR_In, RAM_Out, RAM_In, PC_Out);
  and and_2 (and_2_out, nor_2_out, nor_3_out);
  assign controlled_buffer_1_out[3] = A_Out ? A_q3 : 1'bz;  // Controlled_Buffer controlled_buffer_14
  assign controlled_buffer_1_out[4] = A_Out ? A_2_q0 : 1'bz;  // Controlled_Buffer controlled_buffer_15
  assign controlled_buffer_1_out[5] = A_Out ? A_2_q1 : 1'bz;  // Controlled_Buffer controlled_buffer_16
  Full_Adder Adder_2 (
    .A0(A_2_q0), .B0(xor_6_out), .C_In(C), .A1(A_2_q1), .B1(xor_8_out), .A2(A_2_q2), .B2(xor_7_out),
    .A3(A_2_q3), .B3(xor_5_out), .S0(Adder_2_s0), .S1(Adder_2_s1), .S2(Adder_2_s2), .S3(Adder_2_s3),
    .C_Out(Adder_2_c_out));
  xor xor_6 (xor_6_out, Sub, B_2_q0);
  xor xor_7 (xor_7_out, Sub, B_2_q2);
  xor xor_8 (xor_8_out, Sub, B_2_q1);
  ROM #(.dataWidth(16)) rom_1 (.addr({IR_2_q0, Microstep_Counter_q0}), .data(rom_1_data), .sel(1'b1));
  assign controlled_buffer_1_out[6] = A_Out ? A_2_q2 : 1'bz;  // Controlled_Buffer controlled_buffer_17
  assign controlled_buffer_1_out[7] = A_Out ? A_2_q3 : 1'bz;  // Controlled_Buffer controlled_buffer_18
  Register ALU_Temp (
    .D0(Adder_2_s0), .Write(ALU_Temp_In), .D1(Adder_2_s1), .D2(Adder_2_s2), .D3(Adder_2_s3),
    .Q0(ALU_Temp_q0), .Zero(Reset), .Q1(ALU_Temp_q1), .Q2(ALU_Temp_q2), .Q3(ALU_Temp_q3));
  assign {controlled_buffer_9_out, Sub, ALU_Temp_Out, ALU_Temp_In, Opperand_Out, IR_In, PC_Count, PC_Out, Out_In, B_In, A_Out, A_In, MAR_In, RAM_Out, RAM_In} = nor_1_out ? rom_1_data : 16'bz;  // Controlled_Buffer controlled_buffer_19
  Decoder #(.select(2), .disabled(0), .enable("false")) decoder_2 (
    .out1(decoder_2_out1), .out2(decoder_2_out2), .out3(decoder_2_out3), .sel(controlled_buffer_9_out));  // open: out0
  or or_3 (or_3_out, ALU_Temp_2_q3, ALU_Temp_2_q2, ALU_Temp_2_q1, ALU_Temp_2_q0);
  Register ALU_Temp_2 (
    .D0(Adder_s0), .Write(ALU_Temp_In), .D1(Adder_s1), .D2(Adder_s2), .D3(Adder_s3), .Q0(ALU_Temp_2_q0),
    .Zero(Reset), .Q1(ALU_Temp_2_q1), .Q2(ALU_Temp_2_q2), .Q3(ALU_Temp_2_q3));
  or or_4 (or_4_out, ALU_Temp_q3, ALU_Temp_q2, ALU_Temp_q1, ALU_Temp_q0);
  nor nor_4 (nor_4_out, or_4_out, or_3_out);
  Register Out (
    .D0(controlled_buffer_1_out[4]), .Write(Out_In), .D1(controlled_buffer_1_out[5]),
    .D2(controlled_buffer_1_out[6]), .D3(controlled_buffer_1_out[7]), .Q0(Out_q0[0]), .Zero(Reset),
    .Q1(Out_q0[1]), .Q2(Out_q0[2]), .Q3(Out_q0[3]));
  Hex_Digit_Display hex_digit_display_2 (.value(Out_q0));  // open: dp
  Register Out_2 (
    .D0(controlled_buffer_1_out[0]), .Write(Out_In), .D1(controlled_buffer_1_out[1]),
    .D2(controlled_buffer_1_out[2]), .D3(controlled_buffer_1_out[3]), .Q0(Out_2_q0[0]), .Zero(Reset),
    .Q1(Out_2_q0[1]), .Q2(Out_2_q0[2]), .Q3(Out_2_q0[3]));
  assign controlled_buffer_1_out[0] = ALU_Temp_Out ? ALU_Temp_2_q0 : 1'bz;  // Controlled_Buffer controlled_buffer_20
  assign controlled_buffer_1_out[1] = ALU_Temp_Out ? ALU_Temp_2_q1 : 1'bz;  // Controlled_Buffer controlled_buffer_21
  assign controlled_buffer_1_out[2] = ALU_Temp_Out ? ALU_Temp_2_q2 : 1'bz;  // Controlled_Buffer controlled_buffer_22
  assign controlled_buffer_1_out[4] = ALU_Temp_Out ? ALU_Temp_q0 : 1'bz;  // Controlled_Buffer controlled_buffer_23
  assign controlled_buffer_1_out[5] = ALU_Temp_Out ? ALU_Temp_q1 : 1'bz;  // Controlled_Buffer controlled_buffer_24
  assign controlled_buffer_1_out[6] = ALU_Temp_Out ? ALU_Temp_q2 : 1'bz;  // Controlled_Buffer controlled_buffer_25
  assign controlled_buffer_1_out[7] = ALU_Temp_Out ? ALU_Temp_q3 : 1'bz;  // Controlled_Buffer controlled_buffer_26
  Hex_Digit_Display hex_digit_display_3 (.value(Out_2_q0));  // open: dp
  nand nand_1 (Halt, RAM_In, RAM_Out);
  and and_3 (and_3_out, decoder_2_out2, Zero);
  and and_4 (and_4_out, decoder_2_out3, Carry);
  assign controlled_buffer_1_out[3] = ALU_Temp_Out ? ALU_Temp_2_q3 : 1'bz;  // Controlled_Buffer controlled_buffer_27
  or or_5 (PC_In, decoder_2_out1, and_3_out, and_4_out);
  // Probe on controlled_buffer_1_out
  RAM #(.addrWidth(4), .bus("asynch")) ram_2 ();  // open: addr, data, sel, ld, clr

  // Notes on the sheet:
  //   Instruction Set:
  //   0x0 LDI VALUE
  //   0x1 STM ADDR
  //   0x2 LDM ADDR
  //   0x3 LDMA
  //   0x4 ADDI VALUE
  //   0x5 SUBI VALUE
  //   0x6 ADDM ADDR
  //   0x7 SUBM ADDR
  //   0x8 JMPI ADDR
  //   0x9 JMPM ADDR
  //   0xA JMPA
  //   0xB JMPMA
  //   0xC JZI ADDR
  //   0xD JCI ADDR
  //   0xE OUT
  //   0xF HLT
  //   contents of rom_1 (hex, n*v repeats v):
  //   0 0 408 15*0 404 11 14*0 404 a 14*0 14 a 14*0 c20 1008 14*0 2c20 1008 14*0 404 822 1008 13*0 404
  //   2822 1008 13*0 4400 15*0 404 4002 14*0 4010 15*0 14 4002 14*0 8400 15*0 c400 15*0 50 15*0 3
endmodule

module Register (
  input  D0,
  input  Write,
  input  Zero,
  input  D1,
  input  D2,
  input  D3,
  output Q0,
  output Q1,
  output Q2,
  output Q3
);

  Register_part #(.width(1), .trigger("high")) register_1 (.D(D0), .Q(Q0), .clk(Write), .clr(Zero));  // open: en
  Register_part #(.width(1), .trigger("high")) register_2 (.D(D1), .Q(Q1), .clk(Write), .clr(Zero));  // open: en
  Register_part #(.width(1), .trigger("high")) register_3 (.D(D2), .Q(Q2), .clk(Write), .clr(Zero));  // open: en
  Register_part #(.width(1), .trigger("high")) register_4 (.D(D3), .Q(Q3), .clk(Write), .clr(Zero));  // open: en
endmodule

module Full_Adder (
  input  A0,
  input  B0,
  input  C_In,
  input  A1,
  input  B1,
  input  A2,
  input  B2,
  input  A3,
  input  B3,
  output S0,
  output S1,
  output S2,
  output S3,
  output C_Out
);

  wire and_1_out, and_2_out, and_3_out, and_4_out, and_5_out, and_6_out, and_7_out, and_8_out, or_1_out,
       or_2_out, or_3_out, xor_1_out, xor_3_out, xor_5_out, xor_7_out;

  xor xor_1 (xor_1_out, A0, B0);
  xor xor_2 (S0, xor_1_out, C_In);
  and and_1 (and_1_out, C_In, xor_1_out);
  and and_2 (and_2_out, B0, A0);
  or or_1 (or_1_out, and_1_out, and_2_out);
  xor xor_3 (xor_3_out, A1, B1);
  xor xor_4 (S1, xor_3_out, or_1_out);
  and and_3 (and_3_out, or_1_out, xor_3_out);
  or or_2 (or_2_out, and_3_out, and_4_out);
  and and_4 (and_4_out, B1, A1);
  xor xor_5 (xor_5_out, A2, B2);
  and and_5 (and_5_out, or_2_out, xor_5_out);
  and and_6 (and_6_out, B2, A2);
  xor xor_6 (S2, xor_5_out, or_2_out);
  or or_3 (or_3_out, and_5_out, and_6_out);
  xor xor_7 (xor_7_out, A3, B3);
  xor xor_8 (S3, xor_7_out, or_3_out);
  and and_7 (and_7_out, or_3_out, xor_7_out);
  and and_8 (and_8_out, B3, A3);
  or or_4 (C_Out, and_7_out, and_8_out);
endmodule

module Counter (
  input  D0,
  input  D1,
  input  D2,
  input  D3,
  input  In,
  input  Zero,
  input  Count,
  output Q0,
  output Q1,
  output Q2,
  output Q3
);

  wire or_1_out;

  Counter_part #(.width(4), .max('hf)) PC (
    .load(In), .D({D3, D2, D1, D0}), .count(Count), .Q({Q3, Q2, Q1, Q0}), .clk(or_1_out), .clr(Zero));  // open: carry
  or or_1 (or_1_out, In, Count);
endmodule
